# Fritzing sketch cablage (saved by Fritzing 0.9.3b)
breadboards: 1

parts:
  Q1 = NPN-Transistor [package="SOT-23 [SMD]"]
  Raspberry_Pi_2 = Raspberry Pi 3 [part_number=RPI-3-V1.2]
  S3 = Round Pushbutton
  S4 = Round Pushbutton
  R4 = Resistor [tolerance=±5% resistance=2.2k package=THT]
  LED4 = LED - 3mm [color="White (4500K)" package="3 mm [THT]"]
  R5 = Resistor [tolerance=±5% resistance=330 package=THT]
  LED5 = LED - 3mm [color="Red (660nm)" package="3 mm [THT]"]
  R6 = Resistor [tolerance=±5% resistance=330 package=THT]
  LED6 = LED - 3mm [color="Yellow (595nm)" package="3 mm [THT]"]
  R7 = Resistor [tolerance=±5% resistance=330 package=THT]

nets:
  N1: Q1.2, Raspberry_Pi_2.GND, S3.leg0, S4.leg1, LED5.cathode, LED6.cathode
  N2: Q1.0, R4.Pin_1
  N3: Q1.1, R5.Pin_0
  N4: Raspberry_Pi_2.GPIO3, S3.leg1
  N5: Raspberry_Pi_2.GIPO17, S4.leg0
  N6: Raspberry_Pi_2.GIPO12, R7.Pin_0
  N7: Raspberry_Pi_2.GIPO18, R4.Pin_0
  N8: Raspberry_Pi_2.GIPO14, R6.Pin_0
  N9: Raspberry_Pi_2.5V, LED4.anode
  N10: LED4.cathode, R5.Pin_1
  N11: LED5.anode, R6.Pin_1
  N12: LED6.anode, R7.Pin_1

notes:
  on/off
  photo
  power
  activity
  activity 2
